// Logisim project WatchLogisim.circ as structural Verilog: 2 circuits, main circuit main
module main (
  input  in_1,
  input  in_2,
  input  in_3,
  input  in_4,
  input  in_5
);

  wire a1, and_1_out, and_8_out, and_9_out, and_10_out, and_11_out, and_12_out, and_13_out, and_14_out,
       and_15_out, and_16_out, and_17_out, and_18_out, and_19_out, and_20_out, and_21_out, and_22_out,
       and_23_out, and_24_out, and_25_out, and_26_out, and_27_out, and_28_out, and_29_out, and_30_out,
       and_31_out, and_32_out, and_34_out, and_35_out, and_36_out, and_37_out, and_38_out, and_39_out,
       and_40_out, and_43_out, and_44_out, and_45_out, and_50_out, and_51_out, and_52_out, and_53_out,
       and_54_out, and_55_out, and_56_out, and_61_out, and_66_out, and_67_out, and_68_out, and_69_out,
       and_70_out, and_71_out, and_72_out, and_73_out, and_74_out, and_75_out, and_76_out, and_77_out,
       button_1_out, button_2_out, button_3_out, button_5_out, controlled_buffer_6_out,
       controlled_buffer_7_out, counter_13_q, counter_17_q, H, i1, i2, i3, \i3_Неправильное , i4, i5,
       \i5_Неправильное , i10, L1, L2, L3, not_1_out, not_3_out, not_5_out, not_6_out, not_7_out, not_8_out,
       not_9_out, or_1_out, or_2_out, or_3_out, or_4_out, or_5_out, or_13_out, or_18_out, or_19_out,
       or_20_out, or_21_out, or_22_out, or_23_out, or_25_out, or_26_out, or_28_out, Q1, Q1_out, Q2, Q2_out,
       Q3, Q3_out, T1, T2, T3, \вр_зв_с , \ЗВУК , \кнAB , \кнB , \кнC , \кнА , \КП1ВЫХ , \КП2ВЫХ , \КП3ВЫХ ,
       \КП4ВЫХ , \КП5ВЫХ , \КП6ВЫХ , \КП7ВЫХ , \КПС1ВЫХ , \КПС2ВЫХ , \КПС3ВЫХ , \КПС4ВЫХ , \сбр_зв_с ,
       \Т1_7_q , \ТГ ;
  wire [0:0] not_2_out;
  wire [2:0] B12, \В2 , \В4 , \В6 , \В8 ;
  wire [3:0] adder_1_out, and_2_out, and_3_out, and_4_out, and_5_out, and_6_out, and_7_out, and_48_out,
       and_49_out, B11, controlled_buffer_1_out, controlled_buffer_2_out, controlled_buffer_3_out,
       controlled_buffer_4_out, controlled_buffer_5_out, counter_5_q, or_7_out, or_8_out, or_9_out,
       or_10_out, \В , \В3 , \В5 , \В7 , \ИП1 , \ИП2 , \ИП3 , \ИП4 , \ИП5 , \ИПС1 , \ИПС2 , \ИПС3 , \ИПС4 ,
       \КП1 , \КП2 ;
  wire [3:3] not_4_out;

  or or_1 (or_1_out, \кнC , button_1_out);
  Button button_1 (.out(button_1_out));
  _7_Segment_Display u_7_segment_display_1 (
    .g(B11[3]), .f(B11[2]), .a(B11[1]), .b(B11[0]), .e(B12[2]), .d(B12[1]), .c(B12[0]));  // open: dp
  not not_1 (not_1_out, L2);
  not not_2 (not_2_out[0], in_4);
  or or_2 (or_2_out, \кнB , button_2_out);
  or or_3 (or_3_out, \кнAB , button_3_out);
  Button button_2 (.out(button_2_out));
  Button button_3 (.out(button_3_out));
  and and_1 (and_1_out, ~or_4_out, or_5_out);  // AND_Gate
  _7_Segment_Display u_7_segment_display_2 (
    .g(\В7 [3]), .f(\В7 [2]), .a(\В7 [1]), .b(\В7 [0]), .e(\В8 [2]), .d(\В8 [1]), .c(\В8 [0]));  // open: dp
  Button button_4 (.out(\кнC ));
  \ИП  \u_ип_1  (
    .a(controlled_buffer_1_out[3]), .b(controlled_buffer_1_out[2]), .c(controlled_buffer_1_out[1]),
    .d(controlled_buffer_1_out[0]), .f1(B11[3]), .f2(B11[2]), .f3(B11[1]), .f4(B11[0]), .f5(B12[2]),
    .f6(B12[1]), .f7(B12[0]));
  assign controlled_buffer_1_out = not_1_out ? adder_1_out : 4'bz;  // Controlled_Buffer controlled_buffer_1
  Adder #(.width(4)) adder_1 (.a(\ИП5 ), .b({in_1, in_2, in_3, not_2_out[0]}), .out(adder_1_out));  // open: cin, cout
  or or_4 (or_4_out, or_3_out, or_2_out);
  or or_5 (or_5_out, a1, or_3_out);
  or or_6 (a1, \кнА , button_5_out);
  Button button_5 (.out(button_5_out));
  _7_Segment_Display u_7_segment_display_3 (
    .g(\В5 [3]), .f(\В5 [2]), .a(\В5 [1]), .b(\В5 [0]), .e(\В6 [2]), .d(\В6 [1]), .c(\В6 [0]));  // open: dp
  Button button_6 (.out(\кнAB ));
  Button button_7 (.out(\кнА ));
  Button button_8 (.out(\кнB ));
  \ИП  \u_ип_2  (
    .a(controlled_buffer_2_out[3]), .b(controlled_buffer_2_out[2]), .c(controlled_buffer_2_out[1]),
    .d(controlled_buffer_2_out[0]), .f1(\В7 [3]), .f2(\В7 [2]), .f3(\В7 [1]), .f4(\В7 [0]), .f5(\В8 [2]),
    .f6(\В8 [1]), .f7(\В8 [0]));
  assign controlled_buffer_2_out = not_3_out ? or_7_out : 4'bz;  // Controlled_Buffer controlled_buffer_2
  assign or_7_out = and_2_out | and_3_out;  // OR_Gate or_7, 4 bits wide
  assign and_2_out = \ИП4  & {4{not_4_out[3]}};  // AND_Gate and_2, 4 bits wide
  _7_Segment_Display u_7_segment_display_4 (
    .g(\В3 [3]), .f(\В3 [2]), .a(\В3 [1]), .b(\В3 [0]), .e(\В4 [2]), .d(\В4 [1]), .c(\В4 [0]));  // open: dp
  \ИП  \u_ип_3  (
    .a(controlled_buffer_3_out[3]), .b(controlled_buffer_3_out[2]), .c(controlled_buffer_3_out[1]),
    .d(controlled_buffer_3_out[0]), .f1(\В5 [3]), .f2(\В5 [2]), .f3(\В5 [1]), .f4(\В5 [0]), .f5(\В6 [2]),
    .f6(\В6 [1]), .f7(\В6 [0]));
  assign controlled_buffer_3_out = not_3_out ? or_8_out : 4'bz;  // Controlled_Buffer controlled_buffer_3
  assign or_8_out = and_5_out | and_4_out;  // OR_Gate or_8, 4 bits wide
  assign and_3_out = \ИПС4  & {4{L3}};  // AND_Gate and_3, 4 bits wide
  _7_Segment_Display u_7_segment_display_5 (
    .g(\В [3]), .f(\В [2]), .a(\В [1]), .b(\В [0]), .e(\В2 [2]), .d(\В2 [1]), .c(\В2 [0]));  // open: dp
  \ИП  \u_ип_4  (
    .a(controlled_buffer_4_out[3]), .b(controlled_buffer_4_out[2]), .c(controlled_buffer_4_out[1]),
    .d(controlled_buffer_4_out[0]), .f1(\В3 [3]), .f2(\В3 [2]), .f3(\В3 [1]), .f4(\В3 [0]), .f5(\В4 [2]),
    .f6(\В4 [1]), .f7(\В4 [0]));
  assign and_4_out = \ИПС3  & {4{L3}};  // AND_Gate and_4, 4 bits wide
  assign and_5_out = \ИП3  & {4{not_4_out[3]}};  // AND_Gate and_5, 4 bits wide
  \ИП  \u_ип_5  (
    .a(controlled_buffer_5_out[3]), .b(controlled_buffer_5_out[2]), .c(controlled_buffer_5_out[1]),
    .d(controlled_buffer_5_out[0]), .f1(\В [3]), .f2(\В [2]), .f3(\В [1]), .f4(\В [0]), .f5(\В2 [2]),
    .f6(\В2 [1]), .f7(\В2 [0]));
  assign controlled_buffer_4_out = not_3_out ? or_9_out : 4'bz;  // Controlled_Buffer controlled_buffer_4
  assign or_9_out = and_7_out | and_6_out;  // OR_Gate or_9, 4 bits wide
  assign and_6_out = \ИПС2  & {4{L3}};  // AND_Gate and_6, 4 bits wide
  assign and_7_out = \ИП2  & {4{not_4_out[3]}};  // AND_Gate and_7, 4 bits wide
  and and_8 (and_8_out, or_5_out, ~or_4_out, ~or_1_out, T3);  // AND_Gate
  and and_9 (and_9_out, or_5_out, ~or_1_out, T3, ~T2);  // AND_Gate
  and and_10 (and_10_out, ~or_5_out, or_4_out, ~or_1_out, ~T1);  // AND_Gate
  and and_11 (and_11_out, ~or_5_out, or_4_out, ~or_1_out, T3, T2);  // AND_Gate
  and and_12 (and_12_out, ~or_5_out, ~or_4_out, or_1_out, T3, T1);  // AND_Gate
  and and_13 (and_13_out, ~or_5_out, ~or_4_out, or_1_out, T3, T2);  // AND_Gate
  and and_14 (and_14_out, or_4_out, ~or_1_out, ~T2, ~T1);  // AND_Gate
  and and_15 (and_15_out, or_5_out, ~or_4_out, ~or_1_out, T2);  // AND_Gate
  and and_16 (and_16_out, or_5_out, ~or_1_out, ~T3, T2);  // AND_Gate
  and and_17 (and_17_out, or_5_out, ~or_4_out, ~or_1_out, ~T3, T1);  // AND_Gate
  and and_18 (and_18_out, ~or_5_out, or_4_out, ~or_1_out, T3, T2);  // AND_Gate
  and and_19 (and_19_out, or_5_out, or_4_out, ~or_1_out, ~T3, ~T1);  // AND_Gate
  and and_20 (and_20_out, ~or_5_out, ~or_4_out, or_1_out, T3, ~T1);  // AND_Gate
  and and_21 (and_21_out, ~or_5_out, ~or_4_out, or_1_out, T2, T1);  // AND_Gate
  and and_22 (and_22_out, ~or_5_out, or_4_out, ~or_1_out, ~T3, ~T2, T1);  // AND_Gate
  and and_23 (and_23_out, ~or_5_out, ~or_4_out, or_1_out, T1);  // AND_Gate
  and and_24 (and_24_out, or_5_out, ~or_1_out, T3, ~T2, T1);  // AND_Gate
  and and_25 (and_25_out, or_5_out, ~or_1_out, ~T3, T2, T1);  // AND_Gate
  and and_26 (and_26_out, ~or_5_out, or_4_out, ~or_1_out, ~T3, ~T2);  // AND_Gate
  and and_27 (and_27_out, ~or_5_out, ~or_4_out, or_1_out, T3, ~T2);  // AND_Gate
  and and_28 (and_28_out, ~or_5_out, ~or_4_out, or_1_out, ~T3, T2);  // AND_Gate
  and and_29 (and_29_out, or_5_out, ~or_4_out, ~or_1_out, T3, T2, ~T1);  // AND_Gate
  and and_30 (and_30_out, or_5_out, ~or_4_out, ~or_1_out, ~T3, ~T2, ~T1);  // AND_Gate
  and and_31 (and_31_out, ~or_5_out, or_4_out, ~or_1_out, T3, T2, T1);  // AND_Gate
  and and_32 (and_32_out, or_5_out, or_4_out, ~or_1_out, ~T3, ~T2, T1);  // AND_Gate
  and and_33 (L1, T3, ~T2, T1);  // AND_Gate
  and and_34 (and_34_out, T3, ~T2, T1);  // AND_Gate
  and and_35 (and_35_out, T3, T2, ~T1);  // AND_Gate
  and and_36 (and_36_out, T3, T2, T1);
  and and_37 (and_37_out, T3, T2, ~T1);  // AND_Gate
  and and_38 (and_38_out, T3, T2, T1);
  and and_39 (and_39_out, or_5_out, ~or_4_out, ~or_1_out, T3, ~T2, ~T1);  // AND_Gate
  and and_40 (and_40_out, or_5_out, ~or_4_out, ~or_1_out, ~T3, T2, T1);  // AND_Gate
  and and_41 (i2, or_5_out, ~or_4_out, ~or_1_out, ~T3, T2, ~T1);  // AND_Gate
  // AND_Gate and_42 has open pins: in0=or_5_out, in1=or_4_out, in2=or_1_out, in3=T3, in4=T2, in5=T1, out=open
  and and_43 (and_43_out, or_5_out, ~or_4_out, ~or_1_out, ~T3, ~T2, T1);  // AND_Gate
  and and_44 (and_44_out, ~or_5_out, ~or_4_out, or_1_out, T3, ~T2, ~T1);  // AND_Gate
  and and_45 (and_45_out, ~or_5_out, ~or_4_out, or_1_out, ~T3, T2, ~T1);  // AND_Gate
  and and_46 (i4, ~or_5_out, or_4_out, ~or_1_out, T3, T2);  // AND_Gate
  and and_47 (\i5_Неправильное , or_5_out, ~or_4_out, ~or_1_out, T3, T2);  // AND_Gate
  LED led_1 (.in(\ЗВУК ));
  LED led_2 (.in(T3));
  LED led_3 (.in(T2));
  LED led_4 (.in(T1));
  assign controlled_buffer_5_out = not_3_out ? or_10_out : 4'bz;  // Controlled_Buffer controlled_buffer_5
  assign or_10_out = and_49_out | and_48_out;  // OR_Gate or_10, 4 bits wide
  assign and_48_out = {4{L3}} & \ИПС1 ;  // AND_Gate and_48, 4 bits wide
  assign and_49_out = \ИП1  & {4{not_4_out[3]}};  // AND_Gate and_49, 4 bits wide
  or u_Q1 (Q1_out, and_8_out, and_9_out, and_10_out, and_11_out, and_12_out, and_13_out, and_14_out);
  or u_Q2 (Q2_out, and_15_out, and_16_out, and_17_out, and_18_out, and_19_out, and_20_out, and_21_out, and_22_out);
  or u_Q3 (Q3_out, and_23_out, and_24_out, and_25_out, and_26_out, and_27_out, and_28_out, and_29_out, and_30_out, and_31_out, and_32_out);
  or or_11 (L2, and_34_out, and_35_out, and_36_out);
  or or_12 (L3, and_37_out, and_38_out);
  and and_50 (and_50_out, ~T3, ~T2, T1, ~Q3, Q2, ~Q1);  // AND_Gate
  and and_51 (and_51_out, ~T3, T2, ~T1, ~Q3, ~Q2, Q1);  // AND_Gate
  and and_52 (and_52_out, Q3, ~Q2, ~Q1, ~T3, T2, T1);  // AND_Gate
  and and_53 (and_53_out, Q3, Q2, ~Q1, and_1_out, T3, T2, T1);  // AND_Gate
  and and_54 (and_54_out, Q3, Q2, Q1, and_1_out, T3, ~T2, T1);  // AND_Gate
  or or_13 (or_13_out, or_1_out, or_4_out, or_5_out);
  or or_14 (i1, and_39_out, and_40_out);
  or or_15 (\i3_Неправильное , and_43_out, and_44_out, and_45_out);
  LED led_5 (.in(\i3_Неправильное ));
  or or_16 (i3, and_50_out, and_51_out, and_52_out);
  or or_17 (i5, and_53_out, and_54_out);
  not not_3 (not_3_out, L1);
  not not_4 (not_4_out[3], L3);
  not not_5 (not_5_out, or_13_out);
  _7_Segment_Display u_7_segment_display_6 (
    .g(B11[3]), .f(B11[2]), .a(B11[1]), .b(B11[0]), .e(B12[2]), .d(B12[1]), .c(B12[0]));  // open: dp
  Counter #(.width(4), .max('hf)) counter_1 (.clk(i2));  // open: load, D, count, Q, carry, clr
  not not_6 (not_6_out, not_5_out);
  _7_Segment_Display u_7_segment_display_7 (
    .g(\В7 [3]), .f(\В7 [2]), .a(\В7 [1]), .b(\В7 [0]), .e(\В8 [2]), .d(\В8 [1]), .c(\В8 [0]));  // open: dp
  Counter #(.width(4), .max('hf)) counter_2 (
    .Q(\ИП5 ), .clk(and_55_out), .clr(\КП7ВЫХ ));  // open: load, D, count, carry
  and and_55 (and_55_out, ~i1, or_19_out);  // AND_Gate
  D_Flip_Flop \u_Т1  (.clk(not_6_out), .D(Q1_out), .Q(T3));  // open: Qn, preset, en, reset
  D_Flip_Flop \u_Т1_2  (.clk(not_6_out), .D(Q2_out), .Q(T2));  // open: Qn, preset, en, reset
  D_Flip_Flop \u_Т1_3  (.clk(not_6_out), .D(Q3_out), .Q(T1));  // open: Qn, preset, en, reset
  _7_Segment_Display u_7_segment_display_8 (
    .g(\В5 [3]), .f(\В5 [2]), .a(\В5 [1]), .b(\В5 [0]), .e(\В6 [2]), .d(\В6 [1]), .c(\В6 [0]));  // open: dp
  Counter #(.width(4), .max('hf)) counter_3 (.clk(i3));  // open: load, D, count, Q, carry, clr
  Counter #(.width(4), .max('hf)) counter_4 (.clk(i5));  // open: load, D, count, Q, carry, clr
  or or_18 (or_18_out, not_6_out, not_6_out);
  Counter #(.width(4), .max('hf)) counter_5 (
    .Q(counter_5_q), .clk(\i3_Неправильное ));  // open: load, D, count, carry, clr
  Counter #(.width(4), .max('hf)) counter_6 (
    .Q(\ИП4 ), .clk(or_21_out), .clr(or_19_out));  // open: load, D, count, carry
  or or_19 (or_19_out, \КП6ВЫХ , H);
  and and_56 (and_56_out, or_20_out, ~i2);  // AND_Gate
  or or_20 (or_20_out, i1, \КП4ВЫХ );
  D_Flip_Flop \u_Т1_4  (.clk(or_18_out), .D(T3), .Q(Q3));  // open: Qn, preset, en, reset
  D_Flip_Flop \u_Т1_5  (.clk(or_18_out), .D(T2), .Q(Q2));  // open: Qn, preset, en, reset
  D_Flip_Flop \u_Т1_6  (.clk(or_18_out), .D(T1), .Q(Q1));  // open: Qn, preset, en, reset
  Pull_Resistor pull_resistor_1 ();  // open: node
  _7_Segment_Display u_7_segment_display_9 (
    .g(\В3 [3]), .f(\В3 [2]), .a(\В3 [1]), .b(\В3 [0]), .e(\В4 [2]), .d(\В4 [1]), .c(\В4 [0]));  // open: dp
  _7_Segment_Display u_7_segment_display_10 (
    .g(\В [3]), .f(\В [2]), .a(\В [1]), .b(\В [0]), .e(\В2 [2]), .d(\В2 [1]), .c(\В2 [0]));  // open: dp
  Counter #(.width(4), .max('hf)) counter_7 (
    .Q(\ИП3 ), .clk(and_56_out), .clr(or_21_out));  // open: load, D, count, carry
  or or_21 (or_21_out, H, \КП5ВЫХ );
  and and_57 (H, and_61_out, \ИП4 [1]);
  and and_58 (\КП6ВЫХ , \ИП4 [0], \ИП4 [1]);
  and and_59 (\КП5ВЫХ , ~\ИП3 [0], \ИП3 [1], ~\ИП3 [2], \ИП3 [3]);  // AND_Gate
  and and_60 (\КП7ВЫХ , \ИП5 [0], \ИП5 [1], \ИП5 [2], ~\ИП5 [3]);  // AND_Gate
  D_Flip_Flop #(.trigger("falling")) \u_Т1_7  (.clk(or_18_out), .D(i10), .Q(\Т1_7_q ));  // open: Qn, preset, en, reset
  not not_7 (not_7_out, \Т1_7_q );
  Counter #(.width(4), .max('hf)) counter_8 (.Q(\ИП2 ), .clk(\КП3ВЫХ ), .clr(\КП4ВЫХ ));  // open: load, D, count, carry
  and and_61 (and_61_out, ~\ИП3 [0], ~\ИП3 [1], \ИП3 [2], ~\ИП3 [3]);  // AND_Gate
  Counter #(.width(4), .max('hf)) counter_9 (
    .Q(\ИП1 ), .clk(or_22_out), .clr(\КП3ВЫХ ));  // open: load, D, count, carry
  or or_22 (or_22_out, i2, \КП2ВЫХ );
  Counter #(.width(4), .max('hf)) counter_10 (
    .Q(\КП2 ), .clk(\КП1ВЫХ ), .clr(\КП2ВЫХ ));  // open: load, D, count, carry
  assign controlled_buffer_6_out = not_8_out ? \ТГ  : 1'bz;  // Controlled_Buffer controlled_buffer_6
  Clock clock_1 (.out(\ТГ ));
  Counter #(.width(4), .max('hf)) counter_11 (
    .Q(\КП1 ), .clk(controlled_buffer_6_out), .clr(\КП1ВЫХ ));  // open: load, D, count, carry
  Counter #(.width(4), .max('hf)) counter_12 (
    .Q(\ИПС4 ), .clk(\КПС3ВЫХ ), .clr(or_23_out));  // open: load, D, count, carry
  or or_23 (or_23_out, \КПС4ВЫХ , i4);
  Counter #(.width(1), .max('h1)) counter_13 (.Q(counter_13_q), .clk(i3));  // open: load, D, count, carry, clr
  and and_62 (\КП1ВЫХ , ~\КП1 [0], \КП1 [1], ~\КП1 [2], \КП1 [3]);  // AND_Gate
  and and_63 (\КП2ВЫХ , ~\КП2 [0], \КП2 [1], \КП2 [2]);  // AND_Gate
  and and_64 (\КП3ВЫХ , ~\ИП1 [0], \ИП1 [1], ~\ИП1 [2], \ИП1 [3]);  // AND_Gate
  and and_65 (\КП4ВЫХ , ~\ИП2 [0], \ИП2 [1], \ИП2 [2]);  // AND_Gate
  or or_24 (\вр_зв_с , and_66_out, and_67_out, and_68_out, and_69_out);
  not not_8 (not_8_out, counter_13_q);
  Counter #(.width(4), .max('hf)) counter_14 (
    .Q(\ИПС3 ), .clk(\КПС2ВЫХ ), .clr(or_25_out));  // open: load, D, count, carry
  or or_25 (or_25_out, \КПС3ВЫХ , i4);
  Counter #(.width(4), .max('hf)) counter_15 (
    .Q(\ИПС2 ), .clk(\КПС1ВЫХ ), .clr(or_26_out));  // open: load, D, count, carry
  or or_26 (or_26_out, \КПС2ВЫХ , i4);
  and and_66 (and_66_out, and_70_out, and_74_out);
  and and_67 (and_67_out, and_71_out, and_75_out);
  and and_68 (and_68_out, and_70_out, and_76_out);
  and and_69 (and_69_out, and_71_out, and_77_out);
  or or_27 (\сбр_зв_с , and_72_out, and_73_out);
  not not_9 (not_9_out, in_5);
  Counter #(.width(4), .max('hf)) counter_16 (
    .Q(\ИПС1 ), .clk(controlled_buffer_7_out), .clr(or_28_out));  // open: load, D, count, carry
  or or_28 (or_28_out, \КПС1ВЫХ , i4);
  and and_70 (and_70_out, ~\ИП1 [0], ~\ИП1 [1], ~\ИП1 [2], ~\ИП1 [3]);  // AND_Gate
  and and_71 (and_71_out, \ИП1 [0], ~\ИП1 [1], \ИП1 [2], ~\ИП1 [3]);  // AND_Gate
  and and_72 (and_72_out, ~\КП1 [0], \КП1 [1], ~\КП1 [2], ~\КП1 [3]);  // AND_Gate
  and and_73 (and_73_out, \КП1 [0], \КП1 [1], \КП1 [2], ~\КП1 [3]);  // AND_Gate
  D_Flip_Flop d_ff_1 (.clk(\вр_зв_с ), .D(not_9_out), .Q(\ЗВУК ), .reset(\сбр_зв_с ));  // open: Qn, preset, en
  and and_74 (and_74_out, ~\ИП2 [0], ~\ИП2 [1], ~\ИП2 [2], ~\ИП2 [3]);  // AND_Gate
  and and_75 (and_75_out, \ИП2 [0], ~\ИП2 [1], ~\ИП2 [2], ~\ИП2 [3]);  // AND_Gate
  and and_76 (and_76_out, \ИП2 [0], \ИП2 [1], ~\ИП2 [2], ~\ИП2 [3]);  // AND_Gate
  and and_77 (and_77_out, ~\ИП2 [0], ~\ИП2 [1], \ИП2 [2], ~\ИП2 [3]);  // AND_Gate
  Counter #(.width(1), .max('h1)) counter_17 (.Q(counter_17_q), .clk(i5));  // open: load, D, count, carry, clr
  and and_78 (\КПС1ВЫХ , ~\ИПС1 [0], \ИПС1 [1], ~\ИПС1 [2], \ИПС1 [3]);  // AND_Gate
  and and_79 (\КПС2ВЫХ , ~\ИПС2 [0], \ИПС2 [1], \ИПС2 [2]);  // AND_Gate
  and and_80 (\КПС3ВЫХ , ~\ИПС3 [0], \ИПС3 [1], ~\ИПС3 [2], \ИПС3 [3]);  // AND_Gate
  and and_81 (\КПС4ВЫХ , ~\ИПС4 [0], \ИПС4 [1], \ИПС4 [2]);  // AND_Gate
  assign controlled_buffer_7_out = counter_17_q ? \ТГ  : 1'bz;  // Controlled_Buffer controlled_buffer_7

  // Other names for the same wires on the sheet: КП3[3:0] = \ИП1 ; КП4[3:0] = \ИП2 ; КП5[3:0] = \ИП3 ;
  //   КП6[3:0] = \ИП4 ; КП7[3:0] = \ИП5 ; КПС1[3:0] = \ИПС1 ; КПС2[3:0] = \ИПС2 ; КПС3[3:0] = \ИПС3 ;
  //   КПС4[3:0] = \ИПС4 

  // Notes on the sheet:
  //   B
  //   A
  //   C  AB  B A
  //   C    AB    B     A
  //   ABC
  //   q1 q2 q3
  //   сброс  при 24
  //   Старший бит снизу
  //   Когда 10 сброс
  //   Когда 6 сброс
  //   0 минут
  //   5 минут
  //   00 минут
  //   10 минут
  //   30 минут
  //   40 минут
  //   10 минут
  //   Минуты
endmodule

module \ИП  (
  input  a,
  input  b,
  input  c,
  input  d,
  output f1,
  output f2,
  output f3,
  output f4,
  output f5,
  output f6,
  output f7
);

  wire and_1_out, and_2_out, and_3_out, and_4_out, and_5_out, and_6_out, and_7_out, and_8_out, and_9_out,
       and_10_out, and_11_out, and_12_out, and_13_out, and_14_out, and_15_out, and_16_out, not_1_out,
       not_2_out, not_3_out, not_4_out, not_5_out, not_6_out, not_7_out, not_8_out, not_9_out, not_10_out,
       not_11_out, not_12_out, not_13_out, not_14_out, not_15_out, not_16_out, not_17_out, not_18_out,
       not_19_out, not_20_out, not_21_out;

  not not_1 (not_1_out, b);
  and and_1 (and_1_out, not_1_out, c);
  and and_2 (and_2_out, b, not_2_out);
  not not_2 (not_2_out, c);
  and and_3 (and_3_out, b, not_3_out);
  not not_3 (not_3_out, d);
  not not_4 (not_4_out, c);
  and and_4 (and_4_out, not_4_out, not_5_out);
  not not_5 (not_5_out, d);
  and and_5 (and_5_out, b, not_6_out);
  not not_6 (not_6_out, c);
  and and_6 (and_6_out, b, not_7_out);
  not not_7 (not_7_out, d);
  not not_8 (not_8_out, b);
  and and_7 (and_7_out, not_8_out, not_9_out);
  not not_9 (not_9_out, d);
  and and_8 (and_8_out, b, d);
  not not_10 (not_10_out, b);
  not not_11 (not_11_out, c);
  and and_9 (and_9_out, not_11_out, not_12_out);
  not not_12 (not_12_out, d);
  and and_10 (and_10_out, c, d);
  not not_13 (not_13_out, b);
  and and_11 (and_11_out, not_13_out, not_14_out);
  not not_14 (not_14_out, d);
  and and_12 (and_12_out, c, not_15_out);
  not not_15 (not_15_out, d);
  not not_16 (not_16_out, b);
  and and_13 (and_13_out, not_16_out, not_17_out);
  not not_17 (not_17_out, d);
  not not_18 (not_18_out, b);
  and and_14 (and_14_out, not_18_out, c);
  and and_15 (and_15_out, c, not_19_out);
  not not_19 (not_19_out, d);
  and and_16 (and_16_out, b, not_20_out, d);
  not not_20 (not_20_out, c);
  not not_21 (not_21_out, c);
  or or_1 (f7, not_21_out, d, b);
  or or_2 (f1, and_1_out, and_2_out, and_3_out, a);
  or or_3 (f2, and_4_out, and_5_out, and_6_out, a);
  or or_4 (f3, and_7_out, c, and_8_out, a);
  or or_5 (f4, not_10_out, and_9_out, and_10_out);
  or or_6 (f5, and_11_out, and_12_out);
  or or_7 (f6, and_13_out, and_14_out, and_15_out, and_16_out, a);
endmodule
